# Fritzing sketch SpaceShooter (saved by Fritzing 0.9.3b)
breadboards: 1

parts:
  Part1 = Arduino Uno (Rev3)
  Part2 = Adafruit Mini TFT Display - 0.96in 160x80 [part_number="Adafruit 3533"]
  microSD1 = MicroSD Card Module
  S1 = Pushbutton [package="[SMD]"]
  S2 = Pushbutton [package="[SMD]"]
  S3 = Pushbutton [package="[SMD]"]
  J1 = Piezo Speaker
  R1 = Resistor [tolerance=±5% resistance=220 package=THT]
  R2 = Resistor [tolerance=±5% resistance=220 package=THT]
  R3 = Resistor [tolerance=±5% resistance=220 package=THT]
  R4 = Resistor [tolerance=±5% resistance=220 package=THT]

nets:
  N1: Part1.D8, Part2.DC
  N2: Part1.D9_PWM, Part2.RES
  N3: Part1.D10_PWM/SS, microSD1.CS
  N4: Part1.D11_PWM/MOSI, Part2.SDA, microSD1.MOSI
  N5: Part1.D12/MISO, microSD1.MISO
  N6: Part1.D13/SCK, Part2.SCL, microSD1.SCK
  N7: Part1.D2, S2.Pin_3, S2.Pin_4, R1.Pin_0
  N8: Part1.D3_PWM, S3.Pin_3, S3.Pin_4, R2.Pin_0
  VCC: Part1.D5_PWM, Part1.5V, Part2.VCC, microSD1.VCC, S1.Pin_1, S1.Pin_2, S2.Pin_1, S2.Pin_2, S3.Pin_1, S3.Pin_2
  N9: Part1.D6_PWM, J1.pin2
  N10: Part1.D7, Part2.CS
  GND: Part1.GND, Part2.GND, microSD1.GND, R1.Pin_1, R2.Pin_1, R3.Pin_0, R4.Pin_0
  N11: S1.Pin_3, S1.Pin_4, R3.Pin_1
  N12: J1.pin1, R4.Pin_1

custom parts:
  Adafruit Mini TFT Display - 0.96in 160x80: It's the size of your thumbnail, with glorious 160x80 pixel color... it's the Adafruit Mini TFT Breakout! This very very small display is only 0.96" diagonal, packed with RGB pixels, for making very small high-density displays. The display uses 4-wire SPI to communicate and has its own pixel-addressable frame buffer, it can be used with every kind of microcontroller. Even a very small one with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
  MicroSD Card Module: A common microSD card module.
